# Fritzing sketch Lab 6 (saved by Fritzing 0.9.1b)
breadboards: 1

parts:
  Part1 = Arduino Nano (Rev3.0)
  S1 = Pushbutton [package="[THT]"]
  C1 = Ceramic Capacitor [capacitance=100nF package="200 mil [THT, multilayer]"]
  LED1 = smd LED [color="Red (633nm)" package="0603 [SMD]"]
  R1 = Resistor [tolerance=±5% resistance=100 package=THT]

nets:
  N1: Part1.GND, S1.Pin_1, S1.Pin_2, C1.0, R1.Pin_1
  N2: Part1.D7, LED1.cathode
  N3: S1.Pin_3, S1.Pin_4, C1.1
  N4: LED1.anode, R1.Pin_0

notes:
  External wires connect to read function generator.
